# Fritzing sketch recording_box (saved by Fritzing 0.9.4)
breadboards: 1

parts:
  Raspberry_Pi_1 = Raspberry Pi 3 [part_number=RPI-3-V1.2]
  U1 = LCD-16X2 [package=lcd-16x2]
  Play = Momentary Switch [package=ksa_sealed_tac_switch]
  Loop/Back = Momentary Switch [package=ksa_sealed_tac_switch]
  Rec = Momentary Switch [package=ksa_sealed_tac_switch]
  Rec_indicator = LED - 5mm [color="Red (633nm)" package="5 mm [THT]"]
  Play_indicator = LED - 5mm [color="Green (555nm)" package="5 mm [THT]"]
  Loop_indicator = LED - 5mm [color="White (4500K)" package="5 mm [THT]"]
  I2C_Display_interface = LCM1602 IIC [part_number="LCM1602 IIC" chip_label="LCM1602 IIC" package="DIP (Dual Inline) [THT]"]
  R1 = Resistor [tolerance=±5% resistance=1k package="2512 [SMD]"]
  R2 = Resistor [tolerance=±5% resistance=1k package="2512 [SMD]"]
  R3 = Resistor [tolerance=±5% resistance=1k package="2512 [SMD]"]
  RTC_module = Adafruit PiRTC PCF8523 [part_number="Adafruit #3386"]
  RotEncoder = Rotary Encoder with Knob

nets:
  3V3: Raspberry_Pi_1.3v3, RTC_module.3.3V
  N1: Raspberry_Pi_1.GPIO2, I2C_Display_interface.SDA, RTC_module.SDA
  N2: Raspberry_Pi_1.GPIO3, I2C_Display_interface.SCL, RTC_module.SCL
  N3: Raspberry_Pi_1.GPIO4, Rec.2
  N4: Raspberry_Pi_1.GPIO17, RotEncoder.no_name_yet#1
  N5: Raspberry_Pi_1.GPIO27, RotEncoder.no_name_yet#4
  N6: Raspberry_Pi_1.GPIO22, Play.2
  N7: Raspberry_Pi_1.GPIO5, Rec_indicator.anode
  N8: Raspberry_Pi_1.GPIO6, Play_indicator.anode
  N9: Raspberry_Pi_1.GPIO13, Loop_indicator.anode
  GND: Raspberry_Pi_1.GND, Play.4, Loop/Back.4, Rec.4, I2C_Display_interface.GND, R1.Pin_1, R2.Pin_1, R3.Pin_1, RTC_module.GND, RotEncoder.no_name_yet#2, RotEncoder.no_name_yet#5
  N10: Raspberry_Pi_1.GPIO23, Loop/Back.2
  N11: Raspberry_Pi_1.GPIO18, RotEncoder.no_name_yet#3
  5V: Raspberry_Pi_1.5V, I2C_Display_interface.VCC
  VSS: U1.VSS, I2C_Display_interface.VSS
  VDD: U1.VDD, I2C_Display_interface.VDD
  N12: U1.VO, I2C_Display_interface.V0
  N13: U1.RS, I2C_Display_interface.RS
  N14: U1.R_W, I2C_Display_interface.RW
  N15: U1.E, I2C_Display_interface.E
  N16: U1.DB0, I2C_Display_interface.D0
  N17: U1.DB1, I2C_Display_interface.D1
  N18: U1.DB2, I2C_Display_interface.D2
  N19: U1.DB3, I2C_Display_interface.D3
  N20: U1.DB4, I2C_Display_interface.D4
  N21: U1.DB5, I2C_Display_interface.D5
  N22: U1.DB6, I2C_Display_interface.D6
  N23: U1.DB7, I2C_Display_interface.D7
  N24: U1.A, I2C_Display_interface.A
  N25: U1.K, I2C_Display_interface.K
  N26: Rec_indicator.cathode, R1.Pin_0
  N27: Play_indicator.cathode, R2.Pin_0
  N28: Loop_indicator.cathode, R3.Pin_0

custom parts:
  LCM1602 IIC: I2C-Module to use a 1602 or 2004 LCD on with the wire.h libory Serial LCD Modul
  Adafruit PiRTC PCF8523: This is a great battery-backed real time clock (RTC) that allows your Raspberry Pi project to keep track of time if the power is lost. Perfect for data-logging, clock-building, time-stamping, timers and alarms, etc. Equipped with PCF8523 RTC, it works great with the Raspberry Pi and has native kernel support. Works perfectly with any Raspberry Pi (or similar single board linux computer)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
  Rotary Encoder with Knob: Rotary Encoder with 1/4" Shaft and Knob
